# Fritzing sketch wiring2 (saved by Fritzing 0.9.3b)
breadboards: 1

parts:
  R1 = Resistor [tolerance=±5% resistance=1k package="1206 [SMD]"]
  Part1 = Arduino Uno (Rev3) - ICSP
  Hall_effect_sensor_(_Speed_sensor_on_at_front_wheel) = HALL-EFFECT [package=sc70]
  U2 = Optocoupler [package=THT]
  oil_pressure = smd LED [color="Red (633nm)" package="0603 [SMD]"]
  right_blinker = smd LED [color="Yellow (595nm)" package="0603 [SMD]"]
  left_blinker = smd LED [color="Yellow (595nm)" package="0603 [SMD]"]
  neutral_switch = smd LED [color="Green (570nm)" package="0603 [SMD]"]
  high_beam_light = smd LED [color="Blue (505nm)" package="0603 [SMD]"]
  R2 = Resistor [tolerance=±5% resistance=1k package="1206 [SMD]"]
  R3 = Resistor [tolerance=±5% resistance=1k package="1206 [SMD]"]
  R4 = Resistor [tolerance=±5% resistance=1k package="1206 [SMD]"]
  R5 = Resistor [tolerance=±5% resistance=1k package="1206 [SMD]"]
  R6 = Resistor [tolerance=±5% resistance=1k package="1206 [SMD]"]
  FUEL_SENSOR = Resistor [tolerance=±5% resistance=220 package="0402 [SMD]"]
  OLED_DISPLAY_128x64 = Grove OLED 128x96  # not connected
  12_V_Motorcycle_battery_through_a_buck_converter = Battery block 9V
  RPM_redline_warning = smd LED [color="Red (660nm)" package="0603 [SMD]"]
  R7 = Resistor [tolerance=±5% resistance=330 package="1206 [SMD]"]
  pull_down_resistor = Resistor [tolerance=±5% resistance=10k package="1206 [SMD]"]
  LM1 = RioRand LM2596
  voltage_divider = Resistor [tolerance=±5% resistance=10k package="0402 [SMD]"]

nets:
  N1: R1.Pin_1, U2.Pin_1
  N2: Part1.A0, FUEL_SENSOR.Pin_0, voltage_divider.Pin_0
  5V: Part1.5V, Hall_effect_sensor_(_Speed_sensor_on_at_front_wheel).VCC, U2.Pin_5, FUEL_SENSOR.Pin_1
  N3: Part1.GND, LM1.Pin_3
  N4: Part1.D2, U2.Pin_4, pull_down_resistor.Pin_0
  N5: Part1.D3_PWM, Hall_effect_sensor_(_Speed_sensor_on_at_front_wheel).OUT
  N6: Part1.D4, R7.Pin_0
  N7: Part1.VIN, LM1.Pin_2
  GND: Hall_effect_sensor_(_Speed_sensor_on_at_front_wheel).GND, oil_pressure.cathode, right_blinker.cathode, left_blinker.cathode, neutral_switch.cathode, high_beam_light.cathode, RPM_redline_warning.cathode, pull_down_resistor.Pin_1, voltage_divider.Pin_1
  N8: oil_pressure.anode, R3.Pin_1
  N9: right_blinker.anode, R6.Pin_1
  N10: left_blinker.anode, R2.Pin_1
  N11: neutral_switch.anode, R4.Pin_1
  N12: high_beam_light.anode, R5.Pin_1
  N13: 12_V_Motorcycle_battery_through_a_buck_converter.-, LM1.Pin_0
  N14: 12_V_Motorcycle_battery_through_a_buck_converter.+, LM1.Pin_1
  N15: RPM_redline_warning.anode, R7.Pin_1
